# Fritzing sketch bsidesparody (saved by Fritzing 0.9.3b)
circuit board: 13.9357cm x 8.64838cm
breadboards: 1

parts:
  U1 = LIPO-110mAh [package=lipo-110]
  S1 = Toggle Switch [package=THT]
  R1 = Resistor [tolerance=±5% resistance=75 package=THT]
  R2 = Resistor [tolerance=±5% resistance=75 package=THT]
  R3 = Resistor [tolerance=±5% resistance=75 package=THT]
  R4 = Resistor [tolerance=±5% resistance=75 package=THT]
  R5 = Resistor [tolerance=±5% resistance=75 package=THT]
  R6 = Resistor [tolerance=±5% resistance=75 package=THT]
  R7 = Resistor [tolerance=±5% resistance=75 package=THT]
  R8 = Resistor [tolerance=±5% resistance=75 package=THT]
  R9 = Resistor [tolerance=±5% resistance=75 package=THT]
  R10 = Resistor [tolerance=±5% resistance=75 package=THT]
  LED6 = LEDs [package=led10mm]
  LED4 = LEDs [package=led10mm]
  LED3 = LEDs [package=led10mm]
  LED2 = LEDs [package=led10mm]
  LED1 = LEDs [package=led10mm]
  LED5 = LEDs [package=led10mm]
  LED10 = LEDs [package=led10mm]
  LED9 = LEDs [package=led10mm]
  LED8 = LEDs [package=led10mm]
  LED7 = LEDs [package=led10mm]

nets:
  N1: U1.+, S1.COM
  N2: U1.-, R1.Pin_0, R2.Pin_0, R3.Pin_0, R4.Pin_0, R5.Pin_0, R6.Pin_0, R7.Pin_0, R8.Pin_0, R9.Pin_0, R10.Pin_0
  N3: S1.L2, LED6.A, LED4.A, LED3.A, LED2.A, LED1.A, LED5.A, LED10.A, LED9.A, LED8.A, LED7.A
  N4: R1.Pin_1, LED1.C
  N5: R2.Pin_1, LED2.C
  N6: R3.Pin_1, LED3.C
  N7: R4.Pin_1, LED4.C
  N8: R5.Pin_1, LED5.C
  N9: R6.Pin_1, LED6.C
  N10: R7.Pin_1, LED7.C
  N11: R8.Pin_1, LED8.C
  N12: R9.Pin_1, LED9.C
  N13: R10.Pin_1, LED10.C

notes:
  THE "SUPER OFFICIAL" PARTY CRASHER BADGE
  I am serious. And don't call me Shirley.
  Surely not affiliated with:
  LEGAL: THIS BADGE DOES NOT EXIST? *Blink twice*
  Glue the 18650 somewhere around here
  This is my first badge design, hope it looks good.
  +
  JLCJLCJLCJLC
  mluZS4gY2hlY2sgb3V0IGh0dHBzOi8vYml0Lmx5LzJYbUp2VzU=
  WW91IHJlYWxseSB0b29rIHRoZSB0aW1lIHRvIGRlY29kZSB0aGlzIGJhc2U2ND8gZ
